// Logisim project boothalgo.circ as structural Verilog: 1 circuit, main circuit main
module main (
  input  [3:0] M,
  input  [3:0] Q,
  output [7:0] out_3,
  output [7:0] out_4,
  output [7:0] out_5,
  output [7:0] Output,
  output [2:0] out_7,
  output [7:0] out_8,
  output [2:0] out_9,
  output [7:0] out_10,
  output [7:0] out_11
);

  wire comparator_1_eq, comparator_1_gt, comparator_1_lt, comparator_2_eq, comparator_2_gt, comparator_2_lt,
       comparator_3_eq, comparator_3_gt, comparator_3_lt, comparator_4_eq, comparator_4_gt, comparator_4_lt;
  wire [2:0] _1_2_out, _1_3_out, _1_4_out, _1_out;
  wire [3:0] multiplexer_1_out, multiplexer_2_out, multiplexer_3_out, multiplexer_4_out, negator_1_out;
  wire [7:0] bit_extender_2_out, bit_extender_3_out, bit_extender_4_out;

  Comparator #(.width(1)) comparator_1 (
    .a(Q[0]), .b(1'b0), .gt(comparator_1_gt), .eq(comparator_1_eq), .lt(comparator_1_lt));
  Comparator #(.width(1)) comparator_2 (
    .a(Q[1]), .b(Q[0]), .gt(comparator_2_gt), .eq(comparator_2_eq), .lt(comparator_2_lt));
  Comparator #(.width(1)) comparator_3 (
    .a(Q[2]), .b(Q[1]), .gt(comparator_3_gt), .eq(comparator_3_eq), .lt(comparator_3_lt));
  Comparator #(.width(1)) comparator_4 (
    .a(Q[3]), .b(Q[2]), .gt(comparator_4_gt), .eq(comparator_4_eq), .lt(comparator_4_lt));
  and _1 (_1_out[0], 1'b1, comparator_1_gt);
  and _0 (_1_out[1], 1'b1, comparator_1_eq);
  and minus_1 (_1_out[2], 1'b1, comparator_1_lt);
  and _1_2 (_1_2_out[0], 1'b1, comparator_2_gt);
  and _0_2 (_1_2_out[1], 1'b1, comparator_2_eq);
  and minus_1_2 (_1_2_out[2], 1'b1, comparator_2_lt);
  and _1_3 (_1_3_out[0], 1'b1, comparator_3_gt);
  and _0_3 (_1_3_out[1], 1'b1, comparator_3_eq);
  and minus_1_3 (_1_3_out[2], 1'b1, comparator_3_lt);
  and _1_4 (_1_4_out[0], 1'b1, comparator_4_gt);
  and _0_4 (_1_4_out[1], 1'b1, comparator_4_eq);
  and minus_1_4 (_1_4_out[2], 1'b1, comparator_4_lt);
  Negator #(.width(4)) negator_1 (.in(M), .out(negator_1_out));
  Multiplexer #(.select(3), .width(4)) multiplexer_1 (
    .in1(M), .in2(4'b0000), .in4(negator_1_out), .out(multiplexer_1_out), .sel(_1_out));  // open: in0, in3, in5, in6, in7, en
  Multiplexer #(.select(3), .width(4)) multiplexer_2 (
    .in1(M), .in2(4'b0000), .in4(negator_1_out), .out(multiplexer_2_out), .sel(_1_2_out));  // open: in0, in3, in5, in6, in7, en
  Multiplexer #(.select(3), .width(4)) multiplexer_3 (
    .in1(M), .in2(4'b0000), .in4(negator_1_out), .out(multiplexer_3_out), .sel(_1_3_out));  // open: in0, in3, in5, in6, in7, en
  Multiplexer #(.select(3), .width(4)) multiplexer_4 (
    .in1(M), .in2(4'b0000), .in4(negator_1_out), .out(multiplexer_4_out), .sel(_1_4_out));  // open: in0, in3, in5, in6, in7, en
  assign out_3 = {{4{1'b0}}, multiplexer_1_out};  // Bit_Extender bit_extender_1
  assign bit_extender_2_out = {{4{1'b0}}, multiplexer_2_out};  // Bit_Extender bit_extender_2
  assign bit_extender_3_out = {{4{1'b0}}, multiplexer_3_out};  // Bit_Extender bit_extender_3
  assign bit_extender_4_out = {{4{1'b0}}, multiplexer_4_out};  // Bit_Extender bit_extender_4
  Shifter shifter_1 (.in(bit_extender_2_out), .\dist (3'b001), .out(out_5));
  Adder #(.width(3)) adder_1 (.a(3'b001), .b(3'b001), .out(out_7));  // open: cin, cout
  Shifter shifter_2 (.in(bit_extender_3_out), .\dist (out_7), .out(out_8));
  Adder #(.width(3)) adder_2 (.a(out_7), .b(3'b001), .out(out_9));  // open: cin, cout
  Adder adder_3 (.a(out_3), .b(out_5), .out(out_4));  // open: cin, cout
  Shifter shifter_3 (.in(bit_extender_4_out), .\dist (out_9), .out(out_11));
  Adder adder_4 (.a(out_8), .b(out_11), .out(out_10));  // open: cin, cout
  Adder adder_5 (.a(out_4), .b(out_10), .out(Output));  // open: cin, cout
endmodule
